// Logisim project logism_Simulation.circ as structural Verilog: 6 circuits, main circuit AU
// Data_in
module ALU (
  input  [15:0] in0,
  input  [15:0] in1,
  input  [5:0] opcode,
  output [3:0] flag,
  output [15:0] Data_out
);

  wire AU_1_c, AU_1_v, not_3_out;
  wire [15:0] AU_1_output, LU_1_out1, multiplexer_1_out, multiplexer_2_out, not_1_out, not_2_out;

  assign not_1_out = ~in0;  // NOT_Gate not_1, 16 bits wide
  assign not_2_out = ~in1;  // NOT_Gate not_2, 16 bits wide
  Multiplexer #(.width(16)) multiplexer_1 (.in0(in0), .in1(not_1_out), .out(multiplexer_1_out), .sel(opcode[5]));
  Multiplexer #(.width(16)) multiplexer_2 (.in0(in1), .in1(not_2_out), .out(multiplexer_2_out), .sel(opcode[4]));
  AU AU_1 (
    .C_in(opcode[3]), .in0(multiplexer_1_out), .in1(multiplexer_2_out), .Output(AU_1_output), .V(AU_1_v),
    .C(AU_1_c));
  LU LU_1 (.in0(multiplexer_1_out), .in1(multiplexer_2_out), .sel(opcode[3:1]), .out1(LU_1_out1));
  not not_3 (not_3_out, opcode[0]);
  and and_1 (flag[0], AU_1_v, not_3_out);
  and and_2 (flag[1], AU_1_c, not_3_out);
  Multiplexer #(.width(16)) multiplexer_3 (.in0(AU_1_output), .in1(LU_1_out1), .out(Data_out), .sel(opcode[0]));
  nor nor_1 (flag[2], Data_out[0], Data_out[1], Data_out[2], Data_out[3], Data_out[4], Data_out[5], Data_out[6], Data_out[7], Data_out[8], Data_out[9], Data_out[10], Data_out[11], Data_out[12], Data_out[13], Data_out[14], Data_out[15]);

  assign flag[3] = Data_out[15];
endmodule

module AU (
  input  C_in,
  input  [15:0] in0,
  input  [15:0] in1,
  output [15:0] Output,
  output V,
  output C
);

  wire adder_1_cout, adder_2_cout, adder_3_cout, adder_4_cout, adder_5_cout, adder_6_cout, adder_7_cout,
       adder_8_cout, adder_9_cout, adder_10_cout, adder_11_cout, adder_12_cout, adder_13_cout, adder_14_cout,
       adder_15_cout;

  Adder #(.width(1)) adder_1 (.a(in0[0]), .b(in1[0]), .out(Output[0]), .cin(C_in), .cout(adder_1_cout));
  Adder #(.width(1)) adder_2 (.a(in0[1]), .b(in1[1]), .out(Output[1]), .cin(adder_1_cout), .cout(adder_2_cout));
  Adder #(.width(1)) adder_3 (.a(in0[2]), .b(in1[2]), .out(Output[2]), .cin(adder_2_cout), .cout(adder_3_cout));
  Adder #(.width(1)) adder_4 (.a(in0[3]), .b(in1[3]), .out(Output[3]), .cin(adder_3_cout), .cout(adder_4_cout));
  Adder #(.width(1)) adder_5 (.a(in0[4]), .b(in1[4]), .out(Output[4]), .cin(adder_4_cout), .cout(adder_5_cout));
  Adder #(.width(1)) adder_6 (.a(in0[5]), .b(in1[5]), .out(Output[5]), .cin(adder_5_cout), .cout(adder_6_cout));
  Adder #(.width(1)) adder_7 (.a(in0[6]), .b(in1[6]), .out(Output[6]), .cin(adder_6_cout), .cout(adder_7_cout));
  Adder #(.width(1)) adder_8 (.a(in0[7]), .b(in1[7]), .out(Output[7]), .cin(adder_7_cout), .cout(adder_8_cout));
  Adder #(.width(1)) adder_9 (.a(in0[8]), .b(in1[8]), .out(Output[8]), .cin(adder_8_cout), .cout(adder_9_cout));
  Adder #(.width(1)) adder_10 (.a(in0[9]), .b(in1[9]), .out(Output[9]), .cin(adder_9_cout), .cout(adder_10_cout));
  Adder #(.width(1)) adder_11 (.a(in0[10]), .b(in1[10]), .out(Output[10]), .cin(adder_10_cout), .cout(adder_11_cout));
  Adder #(.width(1)) adder_12 (.a(in0[11]), .b(in1[11]), .out(Output[11]), .cin(adder_11_cout), .cout(adder_12_cout));
  Adder #(.width(1)) adder_13 (.a(in0[12]), .b(in1[12]), .out(Output[12]), .cin(adder_12_cout), .cout(adder_13_cout));
  Adder #(.width(1)) adder_14 (.a(in0[13]), .b(in1[13]), .out(Output[13]), .cin(adder_13_cout), .cout(adder_14_cout));
  Adder #(.width(1)) adder_15 (.a(in0[14]), .b(in1[14]), .out(Output[14]), .cin(adder_14_cout), .cout(adder_15_cout));
  Adder #(.width(1)) adder_16 (.a(in0[15]), .b(in1[15]), .out(Output[15]), .cin(adder_15_cout), .cout(C));
  xor xor_1 (V, adder_15_cout, C);
endmodule

module LU (
  input  [15:0] in0,
  input  [15:0] in1,
  input  [2:0] sel,
  output [15:0] out1
);

  wire [15:0] and_1_out, not_1_out, not_2_out, or_1_out, xor_1_out;

  assign and_1_out = in0 & in1;  // AND_Gate and_1, 16 bits wide
  assign or_1_out = in0 | in1;  // OR_Gate or_1, 16 bits wide
  assign xor_1_out = in0 ^ in1;  // XOR_Gate xor_1, 16 bits wide
  assign not_1_out = ~and_1_out;  // NOT_Gate not_1, 16 bits wide
  assign not_2_out = ~or_1_out;  // NOT_Gate not_2, 16 bits wide
  Multiplexer #(.select(3), .width(16)) multiplexer_1 (
    .in0(in0), .in1(in1), .in2(and_1_out), .in3(not_1_out), .in4(or_1_out), .in5(not_2_out), .in6(xor_1_out),
    .out(out1), .sel(sel));  // open: in7
endmodule

module ALU_pipelining (
  input  [1:0] in_1,
  input  [15:0] in_2,
  input  [15:0] in_3,
  input  [5:0] in_4
);

  wire binary_count_1_out0, binary_count_1_out1, binary_decoder_1_out0, clock_1_out;
  wire [15:0] alu_1_data_out;

  Clock clock_1 (.out(clock_1_out));
  Binary_count binary_count_1 (.clk(clock_1_out), .out0(binary_count_1_out0), .out1(binary_count_1_out1));
  ALU alu_1 (.in0(in_2), .in1(in_3), .opcode(in_4), .Data_out(alu_1_data_out));  // open: flag
  RAM #(.addrWidth(2), .dataWidth(16)) ram_1 (
    .addr(in_1), .we(binary_decoder_1_out0), .clk(binary_decoder_1_out0), .din(alu_1_data_out));  // open: oe, dout
  Binary_decoder binary_decoder_1 (
    .in0(binary_count_1_out0), .in1(binary_count_1_out1), .out0(binary_decoder_1_out0));  // open: out1, out2, out3
endmodule

module Binary_count (
  input  clk,
  output out0,
  output out1
);

  J_K_Flip_Flop j_k_ff_1 (.J(1'b1), .K(1'b1), .clk(clk), .Q(out0));  // open: Qn, preset, reset
  J_K_Flip_Flop j_k_ff_2 (.J(1'b1), .K(1'b1), .clk(out0), .Q(out1));  // open: Qn, preset, reset
endmodule

module Binary_decoder (
  input  in0,
  input  in1,
  output out0,
  output out1,
  output out2,
  output out3
);

  wire not_1_out, not_2_out;

  not not_1 (not_1_out, in0);
  not not_2 (not_2_out, in1);
  and and_1 (out0, not_1_out, not_2_out);
  and and_2 (out1, not_1_out, in1);
  and and_3 (out2, in0, not_2_out);
  and and_4 (out3, in1, in0);
endmodule
